// Digital circuit Full circuit.dig as structural Verilog
module Full_circuit (
);

  wire diodebackward_1_out, diodebackward_2_out, diodebackward_3_out, diodebackward_4_out,
       diodebackward_5_out, node_mcu_1_p1, node_mcu_1_p2, node_mcu_1_p3, node_mcu_1_p4, node_mcu_1_p5,
       node_mcu_1_p6, node_mcu_1_p7, node_mcu_1_p8;

  DiodeBackward diodebackward_1 (.in(node_mcu_1_p1), .out(diodebackward_1_out));
  DiodeBackward diodebackward_2 (.in(node_mcu_1_p1), .out(diodebackward_2_out));
  DiodeBackward diodebackward_3 (.in(node_mcu_1_p1), .out(diodebackward_3_out));
  // NODE_MCU node_mcu_1: pin names not known; wires that end beside it: node_mcu_1_p1, node_mcu_1_p2, node_mcu_1_p3, node_mcu_1_p4, node_mcu_1_p5, node_mcu_1_p6, node_mcu_1_p7, node_mcu_1_p8
  Vandsensor vandsensor_1 (.S(diodebackward_2_out), .plus(node_mcu_1_p3), .out_3(node_mcu_1_p8));
  Vandsensor vandsensor_2 (.S(diodebackward_1_out), .plus(node_mcu_1_p5), .out_3(node_mcu_1_p8));
  Hygrometer hygrometer_1 (.plus(node_mcu_1_p6), .out_2(diodebackward_3_out));
  DiodeBackward diodebackward_4 (.in(node_mcu_1_p2), .out(diodebackward_4_out));
  Motor motor_1 (.plus(node_mcu_1_p2), .out_2(diodebackward_4_out));
  Transistor transistor_1 (.COLLECTOR(node_mcu_1_p8), .BASE(node_mcu_1_p4));  // open: EMITTER
  Transistor transistor_2 (.COLLECTOR(node_mcu_1_p8), .BASE(node_mcu_1_p7));  // open: EMITTER
  DiodeBackward diodebackward_5 (.in(node_mcu_1_p2), .out(diodebackward_5_out));
  Motor motor_2 (.plus(node_mcu_1_p2), .out_2(diodebackward_5_out));
  Motor motor_3 (.plus(node_mcu_1_p2), .out_2(diodebackward_5_out));
endmodule
